# Fritzing sketch Circuit (saved by Fritzing 0.9.3b)
breadboards: 1

parts:
  Part1 = Arduino Nano (Rev3.0)  # not connected
  F2 = FUSE [package=fuse_5mm]  # not connected
  DS1 = DS18B20 1-Wire Temperature Sensor [part_number=DS18B20]
  R1 = Resistor [tolerance=±5% resistance=4.7k package="1206 [SMD]"]
  Maluska1 = maluska dil miniaturrelais [part_number="DIL Mini RY" package=THT]

nets:
  N1: DS1.GND, Maluska1.16
  N2: DS1.DQ, R1.Pin_1
  N3: DS1.VDD, R1.Pin_0
